# Fritzing sketch Three i2c devices on PCF8574 (saved by Fritzing 0.9.3b)
breadboards: 3

parts:
  4x4_Matrix_Membrane_Keypad = Keypad Membran 4x4
  ESP32_DevKitC_V4 = ESP32 DevKitc V4
  PCF8574_-_Addr_0x21 = pcf8574 io expansion board [package=THT]
  R1-R8 = Resistor [tolerance=±5% resistance=10k package="0805 [SMD]"]
  R2 = Resistor [tolerance=±5% resistance=10k package="0805 [SMD]"]
  R3 = Resistor [tolerance=±5% resistance=10k package="0805 [SMD]"]
  R4 = Resistor [tolerance=±5% resistance=10k package="0805 [SMD]"]
  R5 = Resistor [tolerance=±5% resistance=10k package="0805 [SMD]"]
  R6 = Resistor [tolerance=±5% resistance=10k package="0805 [SMD]"]
  R7 = Resistor [tolerance=±5% resistance=10k package="0805 [SMD]"]
  R8 = Resistor [tolerance=±5% resistance=10k package="0805 [SMD]"]
  R9 = Resistor [tolerance=±5% resistance=10k package="0805 [SMD]"]
  LED1 = smd LED [color="Orange (620nm)" package="0805 [SMD]"]
  LED2 = smd LED [color="Yellow (592nm)" package="1206 [SMD]"]
  LED3 = smd LED [color="Red (633nm)" package="0603 [SMD]"]
  LED4 = smd LED [color="Green (565nm)" package="1206 [SMD]"]
  LED5 = smd LED [color="Blue (470nm)" package="1206 [SMD]"]
  LED6 = smd LED [color="White (6500K)" package="1206 [SMD]"]
  LED7 = smd LED [color="Orange (620nm)" package="1206 [SMD]"]
  LED8 = smd LED [color="Red (635nm)" package="1206 [SMD]"]
  HW-131_Power_Supply = YwRobot Breadboard Power Supply [part_number=545043]
  PCF8574_-_Addr_0x20 = pcf8574 io expansion board [package=THT]
  LCD_1602_on_PCF8574_-_Addr_0x27 = LCD1602-I2C

nets:
  N1: 4x4_Matrix_Membrane_Keypad.Pin1, PCF8574_-_Addr_0x20.O7
  N2: 4x4_Matrix_Membrane_Keypad.Pin2, PCF8574_-_Addr_0x20.O6
  N3: 4x4_Matrix_Membrane_Keypad.Pin3, PCF8574_-_Addr_0x20.O5
  N4: 4x4_Matrix_Membrane_Keypad.Pin4, PCF8574_-_Addr_0x20.O4
  N5: 4x4_Matrix_Membrane_Keypad.Pin5, PCF8574_-_Addr_0x20.O3
  N6: 4x4_Matrix_Membrane_Keypad.Pin6, PCF8574_-_Addr_0x20.O2
  N7: 4x4_Matrix_Membrane_Keypad.Pin7, PCF8574_-_Addr_0x20.O1
  N8: 4x4_Matrix_Membrane_Keypad.Pin8, PCF8574_-_Addr_0x20.O0
  N9: ESP32_DevKitC_V4.IO15, R9.Pin_0, PCF8574_-_Addr_0x20.INT
  N10: ESP32_DevKitC_V4.IO21, PCF8574_-_Addr_0x21.SDA, PCF8574_-_Addr_0x20.SDA, LCD_1602_on_PCF8574_-_Addr_0x27.SDA
  N11: ESP32_DevKitC_V4.IO22, PCF8574_-_Addr_0x21.SCL, PCF8574_-_Addr_0x20.SCL, LCD_1602_on_PCF8574_-_Addr_0x27.SCL
  GND: ESP32_DevKitC_V4.GND#18, PCF8574_-_Addr_0x21.GND, LED1.cathode, LED2.cathode, LED3.cathode, LED4.cathode, LED5.cathode, LED6.cathode, LED7.cathode, LED8.cathode, HW-131_Power_Supply.GND#13, HW-131_Power_Supply.GND#14, PCF8574_-_Addr_0x20.GND, LCD_1602_on_PCF8574_-_Addr_0x27.GND
  N12: ESP32_DevKitC_V4.3V3, HW-131_Power_Supply.VCC#5, HW-131_Power_Supply.VCC#6
  VCC: PCF8574_-_Addr_0x21.VCC, R9.Pin_1, HW-131_Power_Supply.VCC#9, HW-131_Power_Supply.VCC#10, PCF8574_-_Addr_0x20.VCC, LCD_1602_on_PCF8574_-_Addr_0x27.VCC
  N13: PCF8574_-_Addr_0x21.A2c, PCF8574_-_Addr_0x21.A2-
  N14: PCF8574_-_Addr_0x21.A1c, PCF8574_-_Addr_0x21.A1-
  N15: PCF8574_-_Addr_0x21.A0+, PCF8574_-_Addr_0x21.A0c
  N16: PCF8574_-_Addr_0x21.O0, R2.Pin_0
  N17: PCF8574_-_Addr_0x21.O1, R1-R8.Pin_0
  N18: PCF8574_-_Addr_0x21.O2, R8.Pin_0
  N19: PCF8574_-_Addr_0x21.O3, R7.Pin_0
  N20: PCF8574_-_Addr_0x21.O4, R6.Pin_0
  N21: PCF8574_-_Addr_0x21.O5, R5.Pin_0
  N22: PCF8574_-_Addr_0x21.O6, R4.Pin_0
  N23: PCF8574_-_Addr_0x21.O7, R3.Pin_0
  N24: R1-R8.Pin_1, LED7.anode
  N25: R2.Pin_1, LED8.anode
  N26: R3.Pin_1, LED1.anode
  N27: R4.Pin_1, LED2.anode
  N28: R5.Pin_1, LED4.anode
  N29: R6.Pin_1, LED5.anode
  N30: R7.Pin_1, LED3.anode
  N31: R8.Pin_1, LED6.anode
  N32: HW-131_Power_Supply.GND#11, HW-131_Power_Supply.GND#12
  N33: PCF8574_-_Addr_0x20.A2c, PCF8574_-_Addr_0x20.A2-
  N34: PCF8574_-_Addr_0x20.A1c, PCF8574_-_Addr_0x20.A1-
  N35: PCF8574_-_Addr_0x20.A0c, PCF8574_-_Addr_0x20.A0-

notes:
  Interrupt

custom parts:
  Keypad Membran 4x4: Membrane Keypad 4x4 Matrix
  ESP32 DevKitc V4: ESP32-DevKitC board with ESP32-WROOM-32 module. ESP32-DevKitC V4 is a small-sized ESP32-based development board produced by Espressif. Most of the pins on the ESP module are broken out to the pin headers on the board. The pins D0, D1, D2, D3, CMD and CLK are used internally for communication between ESP32 and SPI flash memory. They are grouped on both sides near the USB connector. Avoid using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
  pcf8574 io expansion board: pcf8574 io expansion board.
  YwRobot Breadboard Power Supply: The YwRobot Breadboard Power Supply (MB-V2) has two power rails; they can be 5V or 3V3. Power to the module can be provided through the female USB socket or through the A10 (female) 2.1mm power jack.
  LCD1602-I2C: A standard character display, usually with 2x16 characters. Comes in many colors with LCM1602 IIC attached.
